# Fritzing sketch projet arroseur (saved by Fritzing 0.9.3b)
breadboards: 1

parts:
  Composant1 = Arduino Uno (Rev3)
  part = Soil Moisture Sensor
  LED1 = LED - 5mm [color="Red (633nm)" package="5 mm [THT]"]
  RHT1 = Humidity and Temperature Sensor RHT03
  R1 = Resistor [tolerance=±5% resistance=470 package="0402 [SMD]"]
  69 = Resistor [tolerance=±5% resistance=470 package="0402 [SMD]"]

nets:
  N1: Composant1.A0, part.SIG
  N2: Composant1.D2, RHT1.Data-signal, 69.Pin_0
  N3: Composant1.D3_PWM, R1.Pin_1
  VCC: Composant1.5V, part.VCC, RHT1.Vcc, 69.Pin_1
  GND: Composant1.GND, part.GND, LED1.cathode, RHT1.GND_2
  N4: LED1.anode, R1.Pin_0

// code stored in the sketch: Untitled.ino

